# Fritzing sketch schematic_fritzing (saved by Fritzing 0.9.3b)
breadboards: 1

parts:
  2N3904 = NPN-Transistor [package="TO92 [THT]"]
  part = Ceramic Capacitor [capacitance=6.8pF package="100 mil [THT, multilayer]"]
  4_8e-6H = Inductor [package="400 mil [THT]"]
  part_2 = Ceramic Capacitor [capacitance=3.3pF package="1206 [SMD, multilayer]"]
  part_3 = Resistor [tolerance=±5% resistance=4.7k package=THT]
  X2 = USB Connectors [package=usb-a-pcb]

nets:
  N1: 2N3904.E, part.0, part_3.Pin_1
  N2: part.1, 4_8e-6H.pin_1, part_2.0
  N3: 4_8e-6H.pin_0, part_2.1, X2.D+
  N4: part_3.Pin_0, X2.VBUS, X2.GND, X2.D-
